# Fritzing sketch howfast_swipe (saved by Fritzing 0.9.3b)
circuit board: 8.46667cm x 5.64444cm

parts:
  Part1 = Adafruit Trinket 5V
  NEOPIXEL1 = Neopixel Strip -- White (60/m)
  R1 = Resistor [tolerance=±5% resistance=10k package="0603 [SMD]"]
  Part2 = GP2Y0D810Z0F
  Part3 = GP2Y0D810Z0F

nets:
  GND: Part1.GND, NEOPIXEL1.GND, Part2.GND, Part3.GND
  N1: Part1.#1, R1.Pin_1
  N2: Part1.#2, Part3.VO
  N3: Part1.#0, Part2.VO
  5V: Part1.VBUS, NEOPIXEL1.+5V, Part2.5V, Part3.5V
  N4: NEOPIXEL1.DI, R1.Pin_0

custom parts:
  Adafruit Trinket 5V: Trinket may be small, but do not be fooled by its size! It's a tiny microcontroller board, built around the Atmel ATtiny85, a little chip with a lot of power. We wanted to design a microcontroller board that was small enough to fit into any project, and low cost enough to use without hesitation. Perfect for when you don't want to give up your expensive dev-board and you aren't willing to take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
  Neopixel Strip -- White (60/m): Neopixel Strip, White, 60 pixels per meter.
